// Logisim project Guia_0502.circ as structural Verilog: 1 circuit, main circuit main
module main (
  input  x,
  input  y,
  output a,
  output b
);

  wire nand_1_out, not_1_out;

  not not_1 (not_1_out, x);
  nand nand_1 (nand_1_out, y, y);
  or or_1 (a, not_1_out, y);
  nand nand_2 (b, x, nand_1_out);

  // Notes on the sheet:
  //   Guia_0502$David de Sa Vieira de Faria$699415
endmodule
